// Logisim project cpu.circ as structural Verilog: 2 circuits, main circuit main
module main (
  input  [31:0] INSTRUCTION,
  input  CLOCK,
  output [31:0] FETCH_ADDRESS,
  output [31:0] s0_Value,
  output [31:0] s1_Value,
  output [31:0] s2_Value,
  output [31:0] ra_Value,
  output [31:0] HI_Value,
  output [31:0] LO_Value
);

  wire MEM_p1, MEM_p5, MEM_p7, MEM_p10, MEM_p13, MEM_p16;
  wire [4:0] writeregister;
  wire [31:0] extend, main_1_read_data_1, main_1_read_data_2, main_2_result, MEM_p8, multiplexer_2_out,
       writedata;

  Register #(.width(32)) PC (.Q(FETCH_ADDRESS), .clk(CLOCK));  // open: D, en, clr
  Register #(.width(32)) LO ();  // open: D, en, Q, clk, clr
  Register #(.width(32)) HI ();  // open: D, en, Q, clk, clr
  assign extend = {{16{1'b0}}, INSTRUCTION[15:0]};  // Bit_Extender bit_extender_1
  regfile_main main_1 (
    .Read_Register_1(INSTRUCTION[25:21]), .Read_Register_2(INSTRUCTION[20:16]),
    .Write_Register(writeregister), .Write_Data(writedata), .Read_Data_1(main_1_read_data_1),
    .Read_Data_2(main_1_read_data_2));  // open: Write_Enable, Clock, s0_Value, s1_Value, s2_Value, ra_Value, in_5
  Multiplexer #(.width(5)) multiplexer_1 (
    .in0(INSTRUCTION[20:16]), .in1(INSTRUCTION[15:11]), .out(writeregister));  // open: sel, en
  Multiplexer #(.width(32)) multiplexer_2 (
    .in0(main_1_read_data_2), .in1(extend), .out(multiplexer_2_out));  // open: sel, en
  alu_main main_2 (
    .X(main_1_read_data_1), .Result(main_2_result), .Y(multiplexer_2_out));  // open: Switch, Equal, Signed_Overflow, Result_2
  maincontrol maincontrol_1 ();  // open: addiu, addi, sb, bne, lhu, beq, lbu, lb, R_Type, jal, lw, andi, swinc, sh, j___jal, lui, ori, sw, slti, instruction, RegDst, Jump, Branch, MemRead, MemToReg, ALUOP, MemWrite, ALUSrc, RegWrite
  // mem_main MEM: pin names not known; wires that end beside it: MEM_p1, MEM_p1, main_2_result, main_1_read_data_2, MEM_p5, MEM_p5, MEM_p7, MEM_p8, MEM_p7, MEM_p10, MEM_p10, HI_Value, MEM_p13, MEM_p13, LO_Value, MEM_p16
  Multiplexer #(.width(32)) multiplexer_3 (.in0(main_2_result), .in1(MEM_p8), .out(writedata));  // open: sel, en

  // Other names for the same wires on the sheet: clk = CLOCK; fetch_addr[31:0] = FETCH_ADDRESS;
  //   readregister2[4:0] = INSTRUCTION[20:16]; readregister1[4:0] = INSTRUCTION[25:21]; ra[31:0] = ra_Value;
  //   s0[31:0] = s0_Value; s1[31:0] = s1_Value; s2[31:0] = s2_Value

  // Notes on the sheet:
  //   Output
  //   These are outputs/inputs from run.circ
  //   Inputs
  //   These are DEBUG/TEST outputs from your circuit.
endmodule

module maincontrol (
  input  [5:0] instruction,
  input  [9:0] addiu,
  input  [9:0] addi,
  input  [9:0] sb,
  input  [9:0] bne,
  input  [9:0] lhu,
  input  [9:0] beq,
  input  [9:0] lbu,
  input  [9:0] lb,
  input  [9:0] R_Type,
  input  [9:0] jal,
  input  [9:0] lw,
  input  [9:0] andi,
  input  [9:0] swinc,
  input  [9:0] sh,
  input  [9:0] j___jal,
  input  [9:0] lui,
  input  [9:0] ori,
  input  [9:0] sw,
  input  [9:0] slti,
  output RegDst,
  output Jump,
  output Branch,
  output MemRead,
  output MemToReg,
  output [1:0] ALUOP,
  output MemWrite,
  output ALUSrc,
  output RegWrite
);

  wire [9:0] multiplexer_1_out, multiplexer_2_out;

  Multiplexer #(.select(5), .width(10)) multiplexer_1 (
    .in0(10'h241), .in2(10'h2), .in3(10'h2), .in5(10'h44), .in8(10'h300), .in9(10'h300), .in10(10'h3b8),
    .in11(10'h180), .in12(10'h380), .in13(10'h340), .in15(10'h318), .out(multiplexer_1_out),
    .sel(instruction[4:0]));  // open: in1, in4, in6, in7, in14, in16, in17, in18, in19, in20, in21, in22, in23, in24, in25, in26, in27, in28, in29, in30, in31, en
  Multiplexer #(.select(5), .width(10)) multiplexer_2 (
    .in0(10'h318), .in3(10'h318), .in5(10'h300), .in8(10'h180), .in9(10'h180), .in10(10'h3b8),
    .in11(10'h180), .in12(10'h80), .in13(10'h340), .in15(10'h318), .out(multiplexer_2_out),
    .sel(instruction[4:0]));  // open: in1, in2, in4, in6, in7, in14, in16, in17, in18, in19, in20, in21, in22, in23, in24, in25, in26, in27, in28, in29, in30, in31, en
  Multiplexer #(.width(10)) multiplexer_3 (
    .in0(multiplexer_1_out), .in1(multiplexer_2_out),
    .out({RegWrite, ALUSrc, MemWrite, ALUOP, MemToReg, MemRead, Branch, Jump, RegDst}), .sel(instruction[5]));  // open: en

  // Other names for the same wires on the sheet: mux1[4:0] = instruction[4:0]
endmodule
